# Fritzing sketch breakout board 40 pin to duel db37 (saved by Fritzing 0.9.3b)
circuit board: 12cm x 6cm
breadboards: 1

parts:
  J2 = ATX24 Pin Power Supply Connector [package=atx24_right_angle]
  J3 = shrouded pin header, 40 pins [form="♂ (shrouded male)"]
  J1 = ATX24 Pin Power Supply Connector [package=atx24_right_angle]

nets:
  N1: J2.1, J3.pin21
  N2: J2.2, J3.pin23
  N3: J2.8, J3.pin28
  N4: J2.9, J3.pin24
  N5: J2.10, J3.pin26
  N6: J2.13, J3.pin32
  N7: J2.14, J3.pin31
  N8: J2.15, J3.pin30
  N9: J2.16, J3.pin29
  N10: J2.17, J3.pin22
  N11: J2.18, J3.pin20
  N12: J2.19, J3.pin19
  N13: J2.21, J3.pin25
  N14: J2.22, J3.pin27
  N15: J2.23, J3.pin13
  N16: J2.24, J3.pin12
  N17: J3.pin1, J1.12, J1.24
  N18: J3.pin2, J1.11, J1.23
  N19: J3.pin3, J1.10, J1.22
  N20: J3.pin5, J1.9, J1.21
  N21: J3.pin7, J1.20
  N22: J3.pin8, J1.19
  N23: J3.pin9, J1.3, J1.15
  N24: J3.pin10, J1.2, J1.14
  N25: J3.pin11, J1.13
  N26: J3.pin33, J1.18
  N27: J3.pin34, J1.17
  N28: J3.pin35, J1.8
  N29: J3.pin36, J1.6
  N30: J3.pin37, J1.7
  N31: J3.pin38, J1.16

custom parts:
  ATX24 Pin Power Supply Connector: ATX24 Pin Power Supply Connector This is a good connector for connecting a computer power supply to a PCB. It's massive, but provides many amps of power at 5V and 12V. SKU: PRT-09498
