# Fritzing sketch schematic v0.1 Final Today (saved by Fritzing 0.9.3b)
circuit board: 10cm x 10cm
breadboards: 1

parts:
  Arduino_Mega_2560 = Arduino Mega 2560 (Rev3) [part_number="Arduino Mega 2560"]
  R2 = Resistor [tolerance=±5% resistance=470 package=THT]
  R4 = Resistor [tolerance=±5% resistance=470 package=THT]
  R6 = Resistor [tolerance=±5% resistance=470 package=THT]
  R8 = Resistor [tolerance=±5% resistance=470 package=THT]
  R9 = Resistor [tolerance=±5% resistance=2.4k package=THT]
  D9 = Rectifier Diode [part_number=1N4004 package="300 mil [THT]"]
  Q1 = Basic FET N-Channel [part_number=STP62NS04Z package="TO220 [THT]"]
  R11 = Resistor [tolerance=±5% resistance=100k package=THT]
  C1 = Ceramic Capacitor [capacitance=0.1µF package="200 mil [THT, multilayer]"]
  C3 = Ceramic Capacitor [capacitance=0.1µF package="200 mil [THT, multilayer]"]
  C5 = Ceramic Capacitor [capacitance=0.1µF package="200 mil [THT, multilayer]"]
  J3 = screw terminal, 2 pins
  R15 = Resistor [tolerance=±5% resistance=2.4k package=THT]
  D11 = Rectifier Diode [part_number=1N4004 package="300 mil [THT]"]
  Q2 = Basic FET N-Channel [part_number=STP62NS04Z package="TO220 [THT]"]
  R16 = Resistor [tolerance=±5% resistance=1k package=THT]
  R17 = Resistor [tolerance=±5% resistance=100k package=THT]
  D10 = Rectifier Diode [part_number=1N4004 package="300 mil [THT]"]
  Q3 = Basic FET N-Channel [part_number=STP62NS04Z package="TO220 [THT]"]
  R13 = Resistor [tolerance=±5% resistance=1k power=0.25W package=THT]
  R14 = Resistor [tolerance=±5% resistance=100k power=0.25W package=THT]
  R18 = Resistor [tolerance=±5% resistance=2.4k package=THT]
  D12 = Rectifier Diode [part_number=1N4004 package="300 mil [THT]"]
  Q4 = Basic FET N-Channel [part_number=STP62NS04Z package="TO220 [THT]"]
  R19 = Resistor [tolerance=±5% resistance=1k package=THT]
  R20 = Resistor [tolerance=±5% resistance=100k package=THT]
  R21 = Resistor [tolerance=±5% resistance=1k package=THT]
  R22 = Resistor [tolerance=±5% resistance=470 package=THT]
  IC1 = IC, DIP package, 8 pins [chip_label=IC part_number=TC4424EPA]
  R23 = Resistor [tolerance=±5% resistance=1k package=THT]
  R24 = Resistor [tolerance=±5% resistance=1k package=THT]
  R25 = Resistor [tolerance=±5% resistance=160 power=2W package=THT]
  R26 = Resistor [tolerance=±5% resistance=2.4k package=THT]
  R27 = Resistor [tolerance=±5% resistance=160 power=2W package=THT]
  R28 = Resistor [tolerance=±5% resistance=2.4k package=THT]
  IC2 = IC, DIP package, 8 pins [chip_label=IC part_number=TC4424EPA]
  R29 = Resistor [tolerance=±5% resistance=1k package=THT]
  R30 = Resistor [tolerance=±5% resistance=1k package=THT]
  R31 = Resistor [tolerance=±5% resistance=160 power=2W package=THT]
  R33 = Resistor [tolerance=±5% resistance=2.4k power=0.25W package=THT]
  R34 = Resistor [tolerance=±5% resistance=2.4k package=THT]
  U1 = Voltage Regulator - 5V [part_number=LM2940T-5.0 package="TO220 [THT]"]
  D15 = Schottky Diode [part_number=1N5818 package="300 mil [THT]"]
  C14 = Tantalum Capacitor [capacitance=47µF voltage=10V package="200 mil [THT, tantalum]"]
  C13 = Ceramic Capacitor [capacitance=0.1µF voltage=50V package="200 mil [THT, multilayer]"]
  C15 = Ceramic Capacitor [capacitance=0.1µF voltage=50V package="200 mil [THT, multilayer]"]
  C16 = Tantalum Capacitor [capacitance=10µF voltage=35V package="200 mil [THT, tantalum]"]
  U2 = V18ZA2P [part_number=ERZV14D220 package=v18za2p]
  R35 = Resistor [tolerance=±5% resistance=100k package=THT]
  R36 = Resistor [tolerance=±5% resistance=100k package=THT]
  R37 = Resistor [tolerance=±5% resistance=100k package=THT]
  R38 = Resistor [tolerance=±5% resistance=100k package=THT]
  VR = IC, DIP package, 8 pins [chip_label="Dual VR Conditioner"]
  JP1 = female pin header, 3 pins [form="♀ (female)"]
  JP2 = female pin header, 3 pins [form="♀ (female)"]
  JP3 = female pin header, 3 pins [form="♀ (female)"]
  R39 = Resistor [tolerance=±5% resistance=1k package=THT]
  JP4 = female pin header, 2 pins [form="♀ (female)"]
  R40 = Resistor [tolerance=±5% resistance=1k package=THT]
  JP5 = female pin header, 2 pins [form="♀ (female)"]
  C18 = Ceramic Capacitor [capacitance=0.3µF package="200 mil [THT, multilayer]"]
  R41 = Resistor [tolerance=±5% resistance=750 package=THT]
  C19 = Ceramic Capacitor [capacitance=0.01µF package="200 mil [THT, multilayer]"]
  R48 = Resistor [tolerance=±5% resistance=100k package=THT]
  R49 = Resistor [tolerance=±5% resistance=100k power=0.25W package=THT]
  R50 = Resistor [tolerance=±5% resistance=1k package=THT]
  R51 = Resistor [tolerance=±5% resistance=1k package=THT]
  R12 = Resistor [tolerance=±5% resistance=2.4k power=0.25W package=THT]
  D16 = Zener Diode [part_number=1N5919BG breakdown_voltage=5.1V package="300 mil [THT]"]
  D17 = Schottky Diode [part_number=1N5818 package="300 mil [THT]"]
  R55 = Resistor [tolerance=±5% resistance=100k package=THT]
  R56 = Resistor [tolerance=±5% resistance=100k power=0.25W package=THT]
  R57 = Resistor [tolerance=±5% resistance=1k package=THT]
  R58 = Resistor [tolerance=±5% resistance=1k package=THT]
  LED5 = LED - 3mm [color="Red (633nm)" package="3 mm [THT]"]
  LED6 = LED - 3mm [color="Red (633nm)" package="3 mm [THT]"]
  LED7 = LED - 3mm [color="Red (633nm)" package="3 mm [THT]"]
  LED8 = LED - 3mm [color="Red (633nm)" package="3 mm [THT]"]
  Q5 = Basic FET N-Channel [part_number=STP62NS04Z package="TO220 [THT]"]
  R32 = Resistor [tolerance=±5% resistance=160 power=2W package=THT]
  Q7 = Basic FET N-Channel [part_number=STP62NS04Z package="TO220 [THT]"]
  Q6 = Basic FET N-Channel [part_number=STP62NS04Z package="TO220 [THT]"]
  LED4 = LED - 3mm [color="Red (633nm)" package="3 mm [THT]"]
  LED3 = LED - 3mm [color="Red (633nm)" package="3 mm [THT]"]
  LED2 = LED - 3mm [color="Red (633nm)" package="3 mm [THT]"]
  LED1 = LED - 3mm [color="Red (633nm)" package="3 mm [THT]"]
  Q8 = Basic FET N-Channel [part_number=STP62NS04Z package="TO220 [THT]"]
  C23 = Ceramic Capacitor [capacitance=4.7nF package="200 mil [THT, multilayer]"]
  J5 = COMPUTER-PERIPHERAL-POWER [package=computer-peripheral-power]
  IC4 = IC, DIP package, 8 pins [chip_label=SP721 part_number=SP721]
  J9 = female pin header, 1 pin [form="♀ (female)"]  # not connected
  J10 = female pin header, 1 pin [form="♀ (female)"]  # not connected
  J11 = female pin header, 1 pin [form="♀ (female)"]  # not connected
  J12 = female pin header, 1 pin [form="♀ (female)"]  # not connected
  J13 = female pin header, 1 pin [form="♀ (female)"]  # not connected
  J14 = female pin header, 1 pin [form="♀ (female)"]
  J15 = female pin header, 1 pin [form="♀ (female)"]
  J16 = female pin header, 1 pin [form="♀ (female)"]
  J17 = female pin header, 1 pin [form="♀ (female)"]
  J18 = female pin header, 1 pin [form="♀ (female)"]  # not connected
  J19 = female pin header, 1 pin [form="♀ (female)"]  # not connected
  J21 = female pin header, 1 pin [form="♀ (female)"]  # not connected
  J22 = female pin header, 1 pin [form="♀ (female)"]  # not connected
  J23 = female pin header, 1 pin [form="♀ (female)"]  # not connected
  J24 = female pin header, 1 pin [form="♀ (female)"]  # not connected
  J25 = female pin header, 1 pin [form="♀ (female)"]  # not connected
  J26 = female pin header, 1 pin [form="♀ (female)"]  # not connected
  J27 = female pin header, 1 pin [form="♀ (female)"]  # not connected
  J28 = female pin header, 1 pin [form="♀ (female)"]  # not connected
  J29 = female pin header, 1 pin [form="♀ (female)"]  # not connected
  J31 = female pin header, 1 pin [form="♀ (female)"]  # not connected
  J32 = female pin header, 1 pin [form="♀ (female)"]  # not connected
  J33 = female pin header, 1 pin [form="♀ (female)"]  # not connected
  J34 = female pin header, 1 pin [form="♀ (female)"]  # not connected
  J35 = female pin header, 1 pin [form="♀ (female)"]  # not connected
  J36 = female pin header, 1 pin [form="♀ (female)"]  # not connected
  J37 = female pin header, 1 pin [form="♀ (female)"]  # not connected
  J38 = female pin header, 1 pin [form="♀ (female)"]  # not connected
  J39 = female pin header, 1 pin [form="♀ (female)"]  # not connected
  J40 = female pin header, 1 pin [form="♀ (female)"]  # not connected
  J41 = female pin header, 1 pin [form="♀ (female)"]  # not connected
  J43 = female pin header, 1 pin [form="♀ (female)"]  # not connected
  J44 = female pin header, 1 pin [form="♀ (female)"]  # not connected
  J45 = female pin header, 1 pin [form="♀ (female)"]  # not connected
  J46 = female pin header, 1 pin [form="♀ (female)"]  # not connected
  J47 = female pin header, 1 pin [form="♀ (female)"]  # not connected
  J48 = female pin header, 1 pin [form="♀ (female)"]  # not connected
  J49 = female pin header, 1 pin [form="♀ (female)"]  # not connected
  J50 = female pin header, 1 pin [form="♀ (female)"]  # not connected
  J51 = female pin header, 1 pin [form="♀ (female)"]  # not connected
  J52 = female pin header, 1 pin [form="♀ (female)"]  # not connected
  J53 = female pin header, 1 pin [form="♀ (female)"]  # not connected
  J55 = female pin header, 1 pin [form="♀ (female)"]  # not connected
  J56 = female pin header, 1 pin [form="♀ (female)"]  # not connected
  J57 = female pin header, 1 pin [form="♀ (female)"]
  J58 = female pin header, 1 pin [form="♀ (female)"]
  J59 = female pin header, 1 pin [form="♀ (female)"]
  J60 = female pin header, 1 pin [form="♀ (female)"]
  J61 = female pin header, 1 pin [form="♀ (female)"]
  J62 = female pin header, 1 pin [form="♀ (female)"]
  J63 = female pin header, 1 pin [form="♀ (female)"]  # not connected
  J64 = female pin header, 1 pin [form="♀ (female)"]  # not connected
  J65 = female pin header, 1 pin [form="♀ (female)"]
  J67 = female pin header, 1 pin [form="♀ (female)"]  # not connected
  J68 = female pin header, 1 pin [form="♀ (female)"]
  J69 = female pin header, 5 pins [form="♀ (female)"]
  DRV8825 = Pololu A4988 [package=SO16]
  J66 = female pin header, 5 pins [form="♀ (female)"]
  MPX4250AP1 = MPX4250AP pressure sensor2 [part_number=MPX]
  C12 = Ceramic Capacitor [capacitance=1µF part_number=CC0805KKX7R7BB105 package="0805 [SMD, multilayer]"]
  C11 = Ceramic Capacitor [capacitance=1µF part_number=CC0805KKX7R7BB105 package="0805 [SMD, multilayer]"]
  C20 = Ceramic Capacitor [capacitance=1µF package="0805 [SMD, multilayer]"]
  R3 = Resistor [tolerance=±0.1% resistance=2.49k part_number=RT0805BRD072K49L package="0805 [SMD]"]
  R1 = Resistor [tolerance=±0.1% resistance=2.49k part_number=RT0805BRD072K49L package="0805 [SMD]"]
  R7 = Resistor [tolerance=±0.1% resistance=3.9k part_number=RC0805FR-073K9L package="0805 [SMD]"]
  R61 = Resistor [tolerance=±5% resistance=220 package="0805 [SMD]"]
  C24 = Ceramic Capacitor [capacitance=0.22µF package="0805 [SMD, multilayer]"]
  R60 = Resistor [tolerance=±5% resistance=1k package="0805 [SMD]"]
  R59 = Resistor [tolerance=±5% resistance=1k package="0805 [SMD]"]
  C25 = Ceramic Capacitor [capacitance=0.01µF package="0805 [SMD, multilayer]"]
  C6 = Ceramic Capacitor [capacitance=0.22µF package="0805 [SMD, multilayer]"]
  C10 = Ceramic Capacitor [capacitance=0.22µF package="0805 [SMD, multilayer]"]
  C4 = Ceramic Capacitor [capacitance=0.22µF package="0805 [SMD, multilayer]"]
  C2 = Ceramic Capacitor [capacitance=0.22µF package="0805 [SMD, multilayer]"]
  C8 = Ceramic Capacitor [capacitance=0.22µF package="0805 [SMD, multilayer]"]
  D18 = Diode [package=sma-diode]
  S1 = SWITCH-DPDT [package=ayz0202]
  R62 = Resistor [tolerance=±1% resistance=120 package="0805 [SMD]"]
  R54 = Resistor [tolerance=±5% resistance=10k package="0805 [SMD]"]
  C9 = Ceramic Capacitor [capacitance=0.1µF package="0805 [SMD, multilayer]"]
  C7 = Ceramic Capacitor [capacitance=0.1µF package="0805 [SMD, multilayer]"]
  SJ1 = Solder Jumper [package=sj_2s-no]  # not connected
  J4 = shrouded pin header, 40 pins [form="♂ (shrouded male)"]
  J70 = female pin header, 5 pins [form="♀ (female)"]
  R10 = Resistor [tolerance=±5% resistance=1k package=THT]

nets:
  ADC Clamp1/O2-CPU-A8: Arduino_Mega_2560.A8, R22.Pin_1, IC4.pin2, C10.1
  N1: Arduino_Mega_2560.A15, J61.pin1
  ADC Clamp6/IAT-CPU-A0: Arduino_Mega_2560.A0, R2.Pin_1, IC4.pin7, C2.1
  ADC Clamp2/CLT-CPU-A1: Arduino_Mega_2560.A1, R4.Pin_1, IC4.pin6, C4.1
  ADC Clamp3/TPS-CPU-A2: Arduino_Mega_2560.A2, R6.Pin_1, IC4.pin1, C6.1
  MAP-CPU-A3: Arduino_Mega_2560.A3, C18.0, R41.Pin_1, J4.pin11
  ADC Clamp4/BRV-CPU-A4: Arduino_Mega_2560.A4, R8.Pin_1, IC4.pin5, C8.1
  SCL-CPU-D21: Arduino_Mega_2560.D21/SCL, Arduino_Mega_2560.SCL, J65.pin1
  TACH1-CPU-D19: Arduino_Mega_2560.D19/RX1, VR.pin8, JP2.pin1, R59.Pin_0, C25.0
  TACH2-CPU-D18: Arduino_Mega_2560.D18/TX1, VR.pin7, JP3.pin3, C24.0
  STEP-CPU-D17: Arduino_Mega_2560.D17_PWM/RX2, DRV8825.STEP
  STEPDIR-CPU-D16: Arduino_Mega_2560.D16_PWM/TX2, DRV8825.DIR
  SDA-CPU-D20: Arduino_Mega_2560.SDA, J59.pin1
  GND: Arduino_Mega_2560.GND, Q1.source, R11.Pin_1, C1.0, C3.0, C5.0, J3.pin1, Q2.source, R17.Pin_1, Q3.source, R14.Pin_1, Q4.source, R20.Pin_1, R21.Pin_1, IC1.pin3, IC2.pin3, U1.GND, C14.-, C13.0, C15.0, C16.-, U2.P$2, R35.Pin_0, R36.Pin_0, R37.Pin_0, R38.Pin_0, VR.pin6, C18.1, C19.0, R48.Pin_0, R49.Pin_0, D16.anode, R55.Pin_0, R56.Pin_0, LED5.cathode, LED6.cathode, LED7.cathode, LED8.cathode, Q5.source, Q7.source, Q6.source, Q8.source, C23.0, IC4.pin4, DRV8825.GND, MPX4250AP1.GND, C12.0, C11.0, C20.0, C24.1, C25.1, C6.0, C10.0, C4.0, C2.0, C8.0, C9.0, C7.0, J4.pin9, J4.pin10, J4.pin12, J4.pin23
  INJ4-CPU-D11: Arduino_Mega_2560.D11_PWM, R19.Pin_0, R20.Pin_0
  INJ3-CPU-D10: Arduino_Mega_2560.D10_PWM, R16.Pin_0, R17.Pin_0
  INJ2-CPU-D9: Arduino_Mega_2560.D9_PWM, R13.Pin_0, R14.Pin_0
  INJ1-CPU-D8: Arduino_Mega_2560.D8_PWM, R11.Pin_0, R10.Pin_0
  5V: Arduino_Mega_2560.IOREF, Arduino_Mega_2560.5V, U1.output_voltage, C14.+, C13.1, VR.pin5, JP1.pin1, R39.Pin_0, R40.Pin_0, C19.1, D16.cathode, D17.cathode, IC4.pin8, J69.pin1, J69.pin2, J69.pin3, J69.pin4, J69.pin5, DRV8825.RESET, DRV8825.SLEEP, MPX4250AP1.Vs, C20.1, R3.Pin_0, R1.Pin_0, R61.Pin_1, D18.C, R62.Pin_0, R54.Pin_0, J4.pin13, J4.pin28, J70.pin1, J70.pin2, J70.pin3, J70.pin4, J70.pin5
  RESET: Arduino_Mega_2560.RESET, D17.anode, C23.1, S1.5
  LC-5-OUT: Arduino_Mega_2560.D2_PWM, R61.Pin_0, D18.A, J4.pin18
  LS2-CPU-D5: Arduino_Mega_2560.D4_PWM, R58.Pin_0
  LS3-CPU-D6: Arduino_Mega_2560.D5_PWM, R50.Pin_0
  LS4-CPU-D4: Arduino_Mega_2560.D6_PWM, R57.Pin_0
  LS1-CPU-D7: Arduino_Mega_2560.D7_PWM, R51.Pin_0
  N2: Arduino_Mega_2560.D24, DRV8825.ENABLE
  IGN2-CPU-D24: Arduino_Mega_2560.D38, R24.Pin_0
  IGN1-CPU-D28: Arduino_Mega_2560.D40, R23.Pin_0
  RST-CPU-D48: Arduino_Mega_2560.D43, J60.pin1
  LC-CPU-D45: Arduino_Mega_2560.D45, J62.pin1
  LC-CPU-D47: Arduino_Mega_2560.D47, J68.pin1
  LC-CPU-D49: Arduino_Mega_2560.D49, J58.pin1
  IGN4-CPU-D36: Arduino_Mega_2560.D50, R30.Pin_0
  LC-CPU-D51: Arduino_Mega_2560.D51, J57.pin1
  IGN3-CPU-D40: Arduino_Mega_2560.D52, R29.Pin_0
  LC-CPU-D53: Arduino_Mega_2560.D53
  IAT Sensor: R2.Pin_0, C1.1, R1.Pin_1, J4.pin20
  CLT Sensor: R4.Pin_0, C3.1, R3.Pin_1, J4.pin19
  TPS Sensor: R6.Pin_0, C5.1, J4.pin22
  N3: R8.Pin_0, R21.Pin_0, R7.Pin_1, C7.1
  12V/12V-raw: R9.Pin_0, J3.pin2, R15.Pin_0, R18.Pin_0, D15.anode, C15.1, C16.+, U2.P$1, JP1.pin3, R12.Pin_0, DRV8825.VMOT, R7.Pin_0
  N4: R9.Pin_1, LED1.anode
  INJ-1-OUT: D9.cathode, Q1.drain, J4.pin1, J4.pin40
  N5: D9.anode, LED1.cathode
  N6: Q1.gate, R10.Pin_1
  N7: R15.Pin_1, LED3.anode
  INJ-3-OUT: D11.cathode, Q2.drain, J4.pin3, J4.pin4
  N8: D11.anode, LED3.cathode
  N9: Q2.gate, R16.Pin_1
  INJ-2-OUT: D10.cathode, Q3.drain, J4.pin2, J4.pin39
  N10: D10.anode, LED2.cathode
  N11: Q3.gate, R13.Pin_1
  N12: R18.Pin_1, LED4.anode
  INJ-4-OUT: D12.cathode, Q4.drain, J4.pin5, J4.pin6
  N13: D12.anode, LED4.cathode
  N14: Q4.gate, R19.Pin_1
  O2 Sensor: R22.Pin_0, C9.1, J4.pin21
  N15: IC1.pin2, R23.Pin_1, R37.Pin_1
  N16: IC1.pin4, R24.Pin_1, R35.Pin_1
  N17: IC1.pin5, R25.Pin_0
  JP1-OUT: IC1.pin6, IC2.pin6, JP1.pin2, C12.1, C11.1
  N18: IC1.pin7, R27.Pin_1
  IGN-2-OUT: R25.Pin_1, R26.Pin_1, J4.pin34
  N19: R26.Pin_0, LED6.anode
  IGN-1-OUT: R27.Pin_0, R28.Pin_1, J4.pin7
  N20: R28.Pin_0, LED5.anode
  N21: IC2.pin2, R29.Pin_1, R38.Pin_1
  N22: IC2.pin4, R30.Pin_1, R36.Pin_1
  N23: IC2.pin5, R32.Pin_0
  N24: IC2.pin7, R31.Pin_1
  IGN-3-OUT: R31.Pin_0, R33.Pin_1, J4.pin33
  N25: R33.Pin_0, LED7.anode
  N26: R34.Pin_0, LED8.anode
  IGN-4-OUT: R34.Pin_1, R32.Pin_1, J4.pin8
  N27: U1.input_voltage, D15.cathode
  VR1-: VR.pin1, J4.pin27
  N28: VR.pin2, JP2.pin3
  N29: VR.pin3, JP3.pin1
  VR2-: VR.pin4, J4.pin26
  VR1+: JP2.pin2, JP4.pin2, J4.pin25
  N30: JP3.pin2, R60.Pin_1
  N31: R39.Pin_1, JP4.pin1
  N32: R40.Pin_1, JP5.pin2
  VR2+: JP5.pin1, R60.Pin_0, J4.pin24
  N33: R41.Pin_0, MPX4250AP1.V_out
  N34: R48.Pin_1, R50.Pin_1, Q7.gate
  N35: R49.Pin_1, R51.Pin_1, Q8.gate
  N36: R12.Pin_1, LED2.anode
  N37: R55.Pin_1, R57.Pin_1, Q5.gate
  N38: R56.Pin_1, R58.Pin_1, Q6.gate
  HC-1-OUT: Q5.drain, J5.NC, J4.pin36
  IDLE-OUT: Q7.drain, J5.12V, J4.pin37
  HC-2-OUT: Q6.drain, J5.GND, J4.pin38
  BOOST-OUT: Q8.drain, J5.5V, J4.pin35
  ADC Clamp5: IC4.pin3, R59.Pin_1
  LC-1-OUT: J14.pin1, J4.pin14
  LC-2-OUT: J15.pin1, J4.pin15
  LC-3-OUT: J16.pin1, J4.pin16
  LC-4-OUT: J17.pin1, J4.pin17
  STEP-1B-OUT: DRV8825.1B, J4.pin32
  STEP-1A-OUT: DRV8825.1A, J4.pin31
  STEP-2A-OUT: DRV8825.2A, J4.pin30
  STEP-2B-OUT: DRV8825.2B, J4.pin29
  N39: J66.pin1, J66.pin2, J66.pin3, J66.pin4, J66.pin5
  N40: S1.4, R54.Pin_1
  N41: S1.6, R62.Pin_1

notes:
  Inlet Air Temperature sensor
  Coolant Temperature Sensor
  Speeduino v0.4, Throttle Position Sensor
  Battery Reference Voltage
  Injector 1
  Speeduino v0.4, Connector 1
  Injector 3
  Injector 2
  Injector 4
  Speeduino v0.4, O2 Sensor
  Ignitor output 1
  Ignitor output 2
  12v
  5v
  Power supply
  IGN Out
  Crank and Cam sensors
  Speeduino v0.2, MAP sensor input
  Based on Speeduino v0.4
  Generic Outputs - High Current
  inj1
  VR
  Hall
  Reset Protection - Refer AVR040 Application note
  ADC Clamping circuit
  Stepper Driver
  PWM Idle / Boost
  GND
  DetonationEMS v0.1
  © Aaron S.
  5V
  Gnd
  A15
  51
  49
  45
  47
  43
  21
  20
  →
  Eth
  Prog
  Run

custom parts:
  MPX4250AP pressure sensor2: MPX4250AP - MPX4250A SERIES Motorola Preferred Device ORIGINAL MANUFACTURER MOUNTING - flat side up Integrated Silicon Pressure Sensor Manifold Absolute Pressure Sensor On-Chip Signal Conditioned, Temperature Compensated and Calibrated The MPX4250A series piezoresistive transducer is a state-of-the-art monolithic silicon pressure sensor designed for a wide range of applications, particularly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
